# Fritzing sketch C-HAT Schematic (saved by Fritzing 0.9.6b)

parts:
  R1 = Resistor [tolerance=±5% resistance=10k power=0.25 package=THT]
  R2 = Resistor [tolerance=±5% resistance=100 power=0.25 package=THT]
  Light_sensor = LTR-301 [package=ltr-301]
  R4 = Resistor [tolerance=±5% resistance=10k power=0.25 package=THT]
  Heartbeat_Sensor = TCRT5000 [package=THT]
  Temperature_sensor = TMP36 [package=to-92]
  Arduino_microcontroller_stacked_with_RTC_board = Adafruit Feather 32u4 Adalogger [part_number="Adafruit #2795"]
  Accelerometer/Magnetometer = LSM303 Breakout Board - Tilt-Compensated Compass

nets:
  VCC: R1.Pin_0, R2.Pin_1, Light_sensor.C, Temperature_sensor.VCC, Arduino_microcontroller_stacked_with_RTC_board.+3V3, Accelerometer/Magnetometer.VCC
  N1: R1.Pin_1, Heartbeat_Sensor.Pin_1, Arduino_microcontroller_stacked_with_RTC_board.A0
  N2: R2.Pin_0, Heartbeat_Sensor.Pin_4
  N3: Light_sensor.E, R4.Pin_1, Arduino_microcontroller_stacked_with_RTC_board.A2
  GND: R4.Pin_0, Heartbeat_Sensor.Pin_2, Heartbeat_Sensor.Pin_3, Temperature_sensor.GND, Arduino_microcontroller_stacked_with_RTC_board.GND, Accelerometer/Magnetometer.GND
  N4: Temperature_sensor.VOUT, Arduino_microcontroller_stacked_with_RTC_board.A1
  N5: Arduino_microcontroller_stacked_with_RTC_board.3, Accelerometer/Magnetometer.SCL_M
  N6: Arduino_microcontroller_stacked_with_RTC_board.2, Accelerometer/Magnetometer.SDA_M

custom parts:
  TCRT5000: TCRT5000 optical reflective sensor
  Adafruit Feather 32u4 Adalogger: This is the Adafruit Feather 32u4 Adalogger - our take on an 'all-in-one' datalogger (or data-reader) with built in USB and battery charging. Its an Adafruit Feather 32u4 with a microSD holder ready to rock! We have other boards in the Feather family, check'em out here At the Feather 32u4's heart is at ATmega32u4 clocked at 8 MHz and at 3.3V logic, a chip setup we've had tons of experience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
