# Fritzing sketch C-HAT Schematic_feeding (saved by Fritzing 1.0.4)

parts:
  R1 = Resistor [tolerance=±5% resistance=10k power=0.25 package=THT]
  R2 = Resistor [tolerance=±5% resistance=100 power=0.25 package=THT]
  Light_sensor = LTR-301 [package=ltr-301]
  Heartbeat_Sensor = TCRT5000 [package=THT]
  Temperature_sensor = TMP36 [package=to-92]
  Arduino_microcontroller_stacked_with_RTC_board = Adafruit Feather 32u4 Adalogger [part_number="Adafruit #2795"]
  C1 = Ceramic Capacitor [capacitance=100nF voltage=50V part_number=C1 package="100 mil [THT, multilayer]"]
  Hall_effect_mandible_sensor = mystery part, 3 pins [chip_label=DRV5053]
  Accelerometer/Magnetometer = Adafruit LIS3MDL + LSM6DS33 - 9 DoF IMU with Accel + Gyro + Mag [part_number="Adafruit #4485"]
  R3 = Resistor [tolerance=±5% power=0.25 resistance=10k package=THT]

nets:
  VCC: R1.Pin_0, R2.Pin_1, Light_sensor.C, Temperature_sensor.VCC, Arduino_microcontroller_stacked_with_RTC_board.+3V3, C1.1, Hall_effect_mandible_sensor.pin1, Accelerometer/Magnetometer.VCC
  N1: R1.Pin_1, Heartbeat_Sensor.Pin_1, Arduino_microcontroller_stacked_with_RTC_board.A0
  N2: R2.Pin_0, Heartbeat_Sensor.Pin_4
  N3: Light_sensor.E, Arduino_microcontroller_stacked_with_RTC_board.A2, R3.Pin_1
  GND: Heartbeat_Sensor.Pin_2, Heartbeat_Sensor.Pin_3, Temperature_sensor.GND, Arduino_microcontroller_stacked_with_RTC_board.GND, C1.0, Hall_effect_mandible_sensor.pin2, Accelerometer/Magnetometer.GND, R3.Pin_0
  N4: Temperature_sensor.VOUT, Arduino_microcontroller_stacked_with_RTC_board.A1
  N5: Arduino_microcontroller_stacked_with_RTC_board.A3, Hall_effect_mandible_sensor.pin3
  N6: Arduino_microcontroller_stacked_with_RTC_board.3, Accelerometer/Magnetometer.SCL
  N7: Arduino_microcontroller_stacked_with_RTC_board.2, Accelerometer/Magnetometer.SDA

custom parts:
  TCRT5000: TCRT5000 optical reflective sensor
  Adafruit Feather 32u4 Adalogger: This is the Adafruit Feather 32u4 Adalogger - our take on an 'all-in-one' datalogger (or data-reader) with built in USB and battery charging. Its an Adafruit Feather 32u4 with a microSD holder ready to rock! We have other boards in the Feather family, check'em out here At the Feather 32u4's heart is at ATmega32u4 clocked at 8 MHz and at 3.3V logic, a chip setup we've had tons of experience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
  Adafruit LIS3MDL + LSM6DS33 - 9 DoF IMU with Accel + Gyro + Mag: Add motion, direction and orientation sensing to your Arduino project with this all-in-one 9 Degree of Freedom (9-DoF) sensor with sensors from ST. This little breakout contains two chips that sit side-by-side to provide 9 degrees of full motion data. The board includes an LSM6DS33, a 6-DoF IMU accelerometer + gyro. The 3-axis accelerometer, can tell you which direction is down towards the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
